// Logisim project branch-comp-harness.circ as structural Verilog: 1 circuit, main circuit main
module main (
  output [7:0] Test,
  output BrEq,
  output BrLt,
  output halt,
  output [31:0] BrData1,
  output [31:0] BrData2,
  output BrUn
);

  wire clock_1_out;
  wire [7:0] adder_1_out;

  Clock clock_1 (.out(clock_1_out));
  Adder adder_1 (.a(8'h1), .b(Test), .out(adder_1_out));  // open: cin, cout
  Register register_1 (.D(adder_1_out), .clk(clock_1_out), .Q(Test));  // open: en, clr
  ROM #(.dataWidth(32)) rom_1 (.addr(Test), .data(BrData1));
  Comparator comparator_1 (.a(Test), .b({8{1'b0}}), .eq(halt));  // open: gt, lt
  // Probe on BrUn
  // Probe on BrData1
  // Probe on BrData1
  ROM #(.dataWidth(32)) rom_2 (.addr(Test), .data(BrData2));
  // branch_comp branch_comp_1: pin names not known; wires that end beside it: BrData1, BrData1, BrUn, BrEq, BrLt
  ROM #(.dataWidth(1)) rom_3 (.addr(Test), .data(BrUn));

  // Notes on the sheet:
  //   Your branch_comp must fit here!
  //   There should be no red or blue wires, and the result should not be all X's
endmodule
