// Logisim project alu-all.circ as structural Verilog: 1 circuit, main circuit main
module main (
  output [7:0] Test,
  output [31:0] ALUResult,
  output halt,
  output [31:0] InputA,
  output [31:0] InputB,
  output [3:0] ALUSel
);

  wire clock_1_out;
  wire [7:0] adder_1_out;

  Clock clock_1 (.out(clock_1_out));
  Adder adder_1 (.a(8'h1), .b(Test), .out(adder_1_out));  // open: cin, cout
  Register register_1 (.D(adder_1_out), .clk(clock_1_out), .Q(Test));  // open: en, clr
  ROM #(.dataWidth(32)) rom_1 (.addr(Test), .data(InputA));
  Comparator comparator_1 (.a(Test), .b(8'h19), .eq(halt));  // open: gt, lt
  // Probe on InputB
  ROM #(.dataWidth(32)) rom_2 (.addr(Test), .data(InputB));
  // Probe on ALUSel
  // Probe on InputA
  // alu alu_1: pin names not known; wires that end beside it: InputA, InputB, ALUSel, ALUResult
  ROM #(.dataWidth(4)) rom_3 (.addr(Test), .data(ALUSel));

  // Notes on the sheet:
  //   contents of rom_1 (hex, n*v repeats v):
  //   ffffffff 5 f234567f f234567f ffffabcd 5 ffff0000 10101010 f234567f f234567f ffff0000 10101010
  //   ffff0000 10101010 f435daa4 72381add f435daa4 72381add f435daa4 72381add 4 ffff0007 f234567f f234567f
  //   88dcd902 f819cd72
  //   Your ALU must fit here!
  //   contents of rom_2 (hex, n*v repeats v):
  //   ffffbeef aa 9 fe9 5 ffffabcd abcd0000 1010 9 fe9 abcd0000 1010 abcd0000 1010 72381add f435daa4
  //   72381add f435daa4 72381add f435daa4 3 ffff0009 9 fe9 1 2
  //   There should be no red or blue wires, and the result should not be all X's
  //   contents of rom_3 (hex, n*v repeats v):
  //   0 0 1 1 2 2 4 4 5 5 6 6 7 7 8 8 9 9 b b c c d d f f
endmodule
